// Logisim project SynthBite16.circ as structural Verilog: 1 circuit, main circuit SynthBite16
module SynthBite16 (
);

  wire AC_p1, AC_p2, AC_p3, AC_p5, AC_p18, AC_p19, AC_p20, AC_p21, AC_p22, AC_p23, AC_p24, AC_p25, AC_p26,
       AC_p27, AC_p28, AC_p29, controlled_buffer_1_out, controlled_buffer_2_out, controlled_buffer_3_out,
       controlled_buffer_4_out, controlled_buffer_5_out, controlled_buffer_6_out, controlled_buffer_7_out,
       controlled_buffer_8_out, controlled_buffer_9_out, controlled_buffer_10_out, controlled_buffer_11_out,
       controlled_buffer_12_out, controlled_buffer_13_out, controlled_buffer_14_out,
       controlled_buffer_15_out, controlled_buffer_16_out, decoder_1_out0, decoder_1_out1, decoder_1_out2,
       decoder_2_out0, decoder_2_out1, decoder_2_out3, MasterClock_out, undriven, undriven_3, undriven_4,
       undriven_5, undriven_6;
  wire [9:0] undriven_2;
  wire [11:0] AC_p6, dipswitch_1_p1;
  wire [15:0] DR_q, MEM_data;
  wire [23:0] CNTRL_MEM_data, register_1_q;

  Clock MasterClock (.out(MasterClock_out));
  Controlled_Buffer controlled_buffer_1 (.out(controlled_buffer_1_out), .en(undriven));  // open: in
  Controlled_Buffer controlled_buffer_2 (.out(controlled_buffer_2_out), .en(undriven));  // open: in
  Controlled_Buffer controlled_buffer_3 (.out(controlled_buffer_3_out), .en(undriven));  // open: in
  Controlled_Buffer controlled_buffer_4 (.out(controlled_buffer_4_out), .en(undriven));  // open: in
  Controlled_Buffer controlled_buffer_5 (.out(controlled_buffer_5_out), .en(undriven));  // open: in
  Controlled_Buffer controlled_buffer_6 (.out(controlled_buffer_6_out), .en(undriven));  // open: in
  Controlled_Buffer controlled_buffer_7 (.out(controlled_buffer_7_out), .en(undriven));  // open: in
  Controlled_Buffer controlled_buffer_8 (.out(controlled_buffer_8_out), .en(undriven));  // open: in
  Controlled_Buffer controlled_buffer_9 (.out(controlled_buffer_9_out), .en(undriven));  // open: in
  Controlled_Buffer controlled_buffer_10 (.out(controlled_buffer_10_out), .en(undriven));  // open: in
  Controlled_Buffer controlled_buffer_11 (.out(controlled_buffer_11_out), .en(undriven));  // open: in
  Controlled_Buffer controlled_buffer_12 (.out(controlled_buffer_12_out), .en(undriven));  // open: in
  Controlled_Buffer controlled_buffer_13 (.out(controlled_buffer_13_out), .en(undriven));  // open: in
  Controlled_Buffer controlled_buffer_14 (.out(controlled_buffer_14_out), .en(undriven));  // open: in
  Controlled_Buffer controlled_buffer_15 (.out(controlled_buffer_15_out), .en(undriven));  // open: in
  Controlled_Buffer controlled_buffer_16 (.out(controlled_buffer_16_out), .en(undriven));  // open: in
  LED led_1 (.in(MasterClock_out));
  Register #(.width(16)) DR (.D(MEM_data), .en(decoder_2_out3), .clk(MasterClock_out), .Q(DR_q));  // open: clr
  DotMatrix #(.matrixcols(16), .matrixrows(1)) dotmatrix_1 (
    .col0(MEM_data[15]), .col1(MEM_data[14]), .col2(MEM_data[13]), .col3(MEM_data[12]), .col4(MEM_data[11]),
    .col5(MEM_data[10]), .col6(MEM_data[9]), .col7(MEM_data[8]), .col8(MEM_data[7]), .col9(MEM_data[6]),
    .col10(MEM_data[5]), .col11(MEM_data[4]), .col12(MEM_data[3]), .col13(MEM_data[2]), .col14(MEM_data[1]),
    .col15(MEM_data[0]));
  // DipSwitch #(.number(12)) dipswitch_1: pin names not known; wires that end beside it: dipswitch_1_p1[0], dipswitch_1_p1[1], dipswitch_1_p1[2], dipswitch_1_p1[3], dipswitch_1_p1[4], dipswitch_1_p1[5], dipswitch_1_p1[6], dipswitch_1_p1[7], dipswitch_1_p1[8], dipswitch_1_p1[9], dipswitch_1_p1[10], dipswitch_1_p1[11]
  ROM #(.addrWidth(10), .dataWidth(24)) CNTRL_MEM (.addr(undriven_2), .data(CNTRL_MEM_data));
  Register #(.width(12)) PC ();  // open: D, en, clk, Q, clr
  Register #(.trigger("falling"), .width(24)) register_1 (
    .D(CNTRL_MEM_data), .en(1'b1), .clk(MasterClock_out), .Q(register_1_q));  // open: clr
  DotMatrix #(.matrixcols(24), .matrixrows(1)) dotmatrix_2 (
    .col0(register_1_q[0]), .col1(register_1_q[1]), .col2(register_1_q[2]), .col3(register_1_q[3]),
    .col4(register_1_q[4]), .col5(register_1_q[5]), .col6(register_1_q[6]), .col7(register_1_q[7]),
    .col8(register_1_q[8]), .col9(register_1_q[9]), .col10(register_1_q[10]), .col11(register_1_q[11]),
    .col12(register_1_q[12]), .col13(register_1_q[13]), .col14(register_1_q[14]), .col15(register_1_q[15]),
    .col16(register_1_q[16]), .col17(register_1_q[17]), .col18(register_1_q[18]), .col19(register_1_q[19]),
    .col20(register_1_q[20]), .col21(register_1_q[21]), .col22(register_1_q[22]), .col23(register_1_q[23]));
  // Shift_Register #(.length(16)) AC: pin names not known; wires that end beside it: AC_p1, AC_p2, AC_p3, MasterClock_out, AC_p5, AC_p6[0], AC_p6[1], AC_p6[2], AC_p6[3], AC_p6[4], AC_p6[5], AC_p6[6], AC_p6[7], AC_p6[8], AC_p6[9], AC_p6[10], AC_p6[11], AC_p18, AC_p19, AC_p20, AC_p21, AC_p22, AC_p23, AC_p24, AC_p25, AC_p26, AC_p27, AC_p28, AC_p29
  RAM #(.addrWidth(12), .asyncread("true"), .dataWidth(16), .databus("bidir")) MEM (
    .addr(dipswitch_1_p1), .we(decoder_2_out1), .oe(decoder_1_out1), .clk(MasterClock_out), .data(MEM_data));
  LED led_2 (.in(decoder_1_out0));
  Decoder #(.enable("false"), .select(4)) decoder_1 (
    .out0(decoder_1_out0), .out1(decoder_1_out1), .out2(decoder_1_out2), .sel(register_1_q[3:0]));  // open: out3, out4, out5, out6, out7, out8, out9, out10, out11, out12, out13, out14, out15
  LED led_3 (.in(decoder_2_out0));
  Decoder #(.enable("false"), .select(4)) decoder_2 (
    .out0(decoder_2_out0), .out1(decoder_2_out1), .out2(AC_p2), .out3(decoder_2_out3), .sel(register_1_q[7:4]));  // open: out4, out5, out6, out7, out8, out9, out10, out11, out12, out13, out14, out15
  assign MEM_data[0] = decoder_1_out2 ? AC_p18 : 1'bz;  // Controlled_Buffer controlled_buffer_17
  assign MEM_data[1] = decoder_1_out2 ? AC_p19 : 1'bz;  // Controlled_Buffer controlled_buffer_18
  assign MEM_data[2] = decoder_1_out2 ? AC_p20 : 1'bz;  // Controlled_Buffer controlled_buffer_19
  assign MEM_data[3] = decoder_1_out2 ? AC_p21 : 1'bz;  // Controlled_Buffer controlled_buffer_20
  assign MEM_data[4] = decoder_1_out2 ? AC_p22 : 1'bz;  // Controlled_Buffer controlled_buffer_21
  assign MEM_data[5] = decoder_1_out2 ? AC_p23 : 1'bz;  // Controlled_Buffer controlled_buffer_22
  assign MEM_data[6] = decoder_1_out2 ? AC_p24 : 1'bz;  // Controlled_Buffer controlled_buffer_23
  assign MEM_data[7] = decoder_1_out2 ? AC_p25 : 1'bz;  // Controlled_Buffer controlled_buffer_24
  assign MEM_data[8] = decoder_1_out2 ? AC_p26 : 1'bz;  // Controlled_Buffer controlled_buffer_25
  assign MEM_data[9] = decoder_1_out2 ? AC_p27 : 1'bz;  // Controlled_Buffer controlled_buffer_26
  assign MEM_data[10] = decoder_1_out2 ? AC_p28 : 1'bz;  // Controlled_Buffer controlled_buffer_27
  assign MEM_data[11] = decoder_1_out2 ? AC_p29 : 1'bz;  // Controlled_Buffer controlled_buffer_28
  assign MEM_data[12] = decoder_1_out2 ? undriven_3 : 1'bz;  // Controlled_Buffer controlled_buffer_29
  assign MEM_data[13] = decoder_1_out2 ? undriven_4 : 1'bz;  // Controlled_Buffer controlled_buffer_30
  assign MEM_data[14] = decoder_1_out2 ? undriven_5 : 1'bz;  // Controlled_Buffer controlled_buffer_31
  assign MEM_data[15] = decoder_1_out2 ? undriven_6 : 1'bz;  // Controlled_Buffer controlled_buffer_32

  // Notes on the sheet:
  //   CLOCK
  //   SYSTEM BUS
  //   16 LINES
  //   PRESENT BUS VALUES
  //   ALU
  //   LEAST SIGNIFICANT LINE
  //   MOST SIGNIFICANT LINE
  //   CONTROL UNIT
  //   ACC SERIAL IN
  //   PRESENT CONTROL
  //   NONE
  //   NONE
  //   DR LOAD
  //   MEM OUT ENABLE
  //   ACC ON BUS
  //   PUT ON BUS
  //   MEM WRITE ENABLE
  //   AC PARLLEL LOAD
  //   AC RESET ASYNC
  //   ACC SHIFT
  //   MAIN MEMORY
  //   LOAD FROM BUS
endmodule
